# Fritzing sketch schema (saved by Fritzing 0.9.3b)

parts:
  U1 = ESP8266 NodeMCU LoLin module
  4_Channel_Relay1 = 4 Channel Power Relay
  4_Channel_Relay2 = 4 Channel Power Relay

nets:
  N1: U1.D0, 4_Channel_Relay2.IN1
  N2: U1.D1, 4_Channel_Relay2.IN2
  N3: U1.D2, 4_Channel_Relay1.IN3, 4_Channel_Relay2.IN3
  N4: U1.D3, 4_Channel_Relay2.IN4
  N5: U1.D4, 4_Channel_Relay1.IN4
  GND: U1.GND, 4_Channel_Relay1.GND, 4_Channel_Relay2.GND
  N6: U1.D5, 4_Channel_Relay1.IN1
  N7: U1.D6, 4_Channel_Relay1.IN2
  N8: U1.VU, 4_Channel_Relay1.VCC
  N9: 4_Channel_Relay1.NO#18, 4_Channel_Relay1.COM#20
  N10: 4_Channel_Relay2.NO#18, 4_Channel_Relay2.COM#20

notes:
  +12V
  DOWN LEFT
  UP LEFT
  LIGHT --> DASHBOARD
  LIGHT --> HEADLIGHT
  BULB
  DOWN RIGHT
  UP RIGHT
  GND
  VCC
  DIN
  CIN

custom parts:
  ESP8266 NodeMCU LoLin module: ESP8266 based NodeMCU
  4 Channel Power Relay: A 4 channel power relay. The module operates at 5V.
